# Fritzing sketch MonitorPinout (saved by Fritzing 0.9.3b)

parts:
  Serial_Port_PM25 = Serial Port Connector
  Raspberry_Pi = Raspberry Pi 3 [part_number=RPI-3-V1.2]
  BME680 = Audio Jack Breakout

nets:
  VCC: Serial_Port_PM25.Vcc, Raspberry_Pi.5V
  GND: Serial_Port_PM25.S1, Raspberry_Pi.GND, BME680.GND
  N1: Serial_Port_PM25.E, Raspberry_Pi.GPIO14
  N2: Serial_Port_PM25.RX_-_Z, Raspberry_Pi.GPIO15
  N3: Raspberry_Pi.3v3, BME680.2-6V
  N4: Raspberry_Pi.GPIO2, BME680.SDA
  N5: Raspberry_Pi.GPIO3, BME680.SCL

notes:
  These Female connection wires connect to the pins out of the back of the BME680 and the
  Serial Port PM25

custom parts:
  Audio Jack Breakout: Replacement: PRT-10588. The new revision corrects the silkscreen so that the pins are now labeled correctly. This page is for reference only. Description: Simple breakout board for the 3.5mm audio jack. Use this breakout (shipped bare) to allow breadboard or SIP access to the super-common 3.5mm audio jack. All five pins are broken out. Note: This is for the bare PCB only. Note: The silkscreen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
